// Digital circuit CPU.dig as structural Verilog
module CPU (
  input  R,
  input  clock
);

  wire alu_1_c, alu_1_n, alu_1_v, alu_1_z, and_1_o, and_2_o, branch_1_jumpen, d_ff_1_nq, d_ff_2_q,
       flags_1_nf, flags_1_vf, flags_1_zf, not_1_o, or_1_o;
  wire [1:0] control_1_out_2;
  wire [3:0] instruction_reader_1_op, instruction_reader_1_ra, instruction_reader_1_rb,
       instruction_reader_1_rd, multiplexer_1_out;
  wire [7:0] registerfile_1_da;
  wire [12:0] control_1_out;
  wire [15:0] alu_1_o, immediate_1_imm, immediate_1_lui, instruction_reader_1_pc_out, ramdualaccess_1_d1,
       ramdualaccess_1_d2, registerfile_1_db, writeback_1_wbdata;
  wire [15:8] registerfile_1_da_2;

  NOT not_1 (.A(clock), .O(not_1_o));
  D_FF d_ff_1 (.D(d_ff_2_q), .C(not_1_o), .nQ(d_ff_1_nq));  // open: Q
  D_FF d_ff_2 (.D(1'b1), .C(clock), .Q(d_ff_2_q));  // open: nQ
  OR or_1 (.A(d_ff_1_nq), .B(R), .O(or_1_o));
  AND and_1 (.A(control_1_out_2[0]), .B(control_1_out_2[1]), .O(and_1_o));
  Instruction_reader instruction_reader_1 (
    .R(or_1_o), .clk(clock), .JMP_ADDR({registerfile_1_da_2, registerfile_1_da}), .JMPE(branch_1_jumpen),
    .WE(1'b1), .Data_in({16{1'b0}}), .STR(1'b0), .STR_ADDR({16{1'b0}}), .INSTR_IN(ramdualaccess_1_d2),
    .OP(instruction_reader_1_op), .RA(instruction_reader_1_ra), .RB(instruction_reader_1_rb),
    .RD(instruction_reader_1_rd), .PC_OUT(instruction_reader_1_pc_out));
  Multiplexer #(.Bits(4)) multiplexer_1 (
    .sel(and_1_o), .in_0(instruction_reader_1_ra), .in_1(instruction_reader_1_rd), .out(multiplexer_1_out));
  immediate immediate_1 (
    .RA(instruction_reader_1_ra), .RB(instruction_reader_1_rb),
    .RDval({registerfile_1_da_2, registerfile_1_da}), .IMM(immediate_1_imm), .LUI(immediate_1_lui));
  RegisterFile #(.AddrBits(4), .Bits(16)) registerfile_1 (
    .Din(writeback_1_wbdata), .we(control_1_out[0]), .Rw(instruction_reader_1_rd), .C(clock),
    .Ra(multiplexer_1_out), .Rb(instruction_reader_1_rb), .Da({registerfile_1_da_2, registerfile_1_da}),
    .Db(registerfile_1_db));
  writeback writeback_1 (
    .ALU(alu_1_o), .MEM(ramdualaccess_1_d1), .IMM(immediate_1_imm), .LUI(immediate_1_lui),
    .WBsrc(control_1_out_2), .WBdata(writeback_1_wbdata));
  control control_1 (.OP(instruction_reader_1_op), .OUT({control_1_out[12:7], control_1_out_2, control_1_out[4:0]}));
  ALU alu_1 (
    .OP(control_1_out[3:1]), .A({registerfile_1_da_2, registerfile_1_da}), .B(registerfile_1_db),
    .Sub(control_1_out[4]), .O(alu_1_o), .N(alu_1_n), .C(alu_1_c), .V(alu_1_v), .Z(alu_1_z));
  flags flags_1 (
    .N(alu_1_n), .C(alu_1_c), .V(alu_1_v), .Z(alu_1_z), .FlagWrite(control_1_out[11]), .CLK(clock),
    .Zf(flags_1_zf), .Nf(flags_1_nf), .Vf(flags_1_vf));  // open: Cf
  RAMDualAccess #(.AddrBits(16), .isProgramMemory("true"), .Bits(16)) ramdualaccess_1 (
    .str(control_1_out[7]), .C(clock), .ld(1'b1), .A1({registerfile_1_da_2, registerfile_1_da}),
    .Din1(registerfile_1_db), .A2(instruction_reader_1_pc_out), .D1(ramdualaccess_1_d1),
    .D2(ramdualaccess_1_d2));
  branch branch_1 (
    .Cond(control_1_out[10:9]), .Zf(flags_1_zf), .Nf(flags_1_nf), .Vf(flags_1_vf), .Branch(control_1_out[8]),
    .JumpEn(branch_1_jumpen));
  AND and_2 (.A(control_1_out[7]), .B(registerfile_1_da_2[15]), .O(and_2_o));
  GraphicCard #(.graphicHeight(10), .graphicWidth(10), .Bits(16)) VRAM (
    .A(registerfile_1_da), .str(and_2_o), .C(clock), .ld(1'b0), .B(1'b0), .D(registerfile_1_db));

  // Notes on the sheet:
  //   clock: Hz: 50
endmodule
